// Logisim project noise_generator.circ as structural Verilog: 1 circuit, main circuit main
module main (
  input  reset
);

  wire counter_1_carry, counter_2_carry, random_1_p1, random_1_p2, rgb_video_1_p1;
  wire [6:0] counter_1_q, counter_2_q;

  Counter #(.max('h7f), .width(7)) counter_1 (
    .count(random_1_p1), .Q(counter_1_q), .carry(counter_1_carry), .clk(random_1_p2), .clr(reset));  // open: load, D, up
  Counter #(.max('h7f), .width(7)) counter_2 (
    .count(counter_1_carry), .Q(counter_2_q), .carry(counter_2_carry), .clk(random_1_p2), .clr(reset));  // open: load, D, up
  // Random random_1: pin names not known; wires that end beside it: random_1_p1, random_1_p2
  Clock clock_1 (.out(random_1_p2));
  // RGB_Video #(.scale(1)) rgb_video_1: pin names not known; wires that end beside it: rgb_video_1_p1, reset, random_1_p2, random_1_p1, counter_1_q, counter_2_q, rgb_video_1_p1
  not not_1 (random_1_p1, counter_2_carry);
endmodule
